// Logisim project processor.circ as structural Verilog
module xor2 (
  input  i_0,
  input  i_1,
  output o
);

  wire and1_out, and2_out, not1_out, not2_out;

  not not1 (not1_out, i_1);
  not not2 (not2_out, i_0);
  and and1 (and1_out, i_0, not1_out);
  and and2 (and2_out, not2_out, i_1);
  or or1 (o, and1_out, and2_out);
endmodule

module xor8 (
  input  a_0,
  input  a_1,
  input  a_2,
  input  a_3,
  input  a_4,
  input  a_5,
  input  a_6,
  input  a_7,
  input  b_0,
  input  b_1,
  input  b_2,
  input  b_3,
  input  b_4,
  input  b_5,
  input  b_6,
  input  b_7,
  output o_0,
  output o_1,
  output o_2,
  output o_3,
  output o_4,
  output o_5,
  output o_6,
  output o_7
);

  xor2 xor2_1 (.i_0(a_0), .i_1(b_0), .o(o_0));
  xor2 xor2_2 (.i_0(a_1), .i_1(b_1), .o(o_1));
  xor2 xor2_3 (.i_0(a_2), .i_1(b_2), .o(o_2));
  xor2 xor2_4 (.i_0(a_3), .i_1(b_3), .o(o_3));
  xor2 xor2_5 (.i_0(a_4), .i_1(b_4), .o(o_4));
  xor2 xor2_6 (.i_0(a_5), .i_1(b_5), .o(o_5));
  xor2 xor2_7 (.i_0(a_6), .i_1(b_6), .o(o_6));
  xor2 xor2_8 (.i_0(a_7), .i_1(b_7), .o(o_7));
endmodule

module and8 (
  input  [7:0] a,
  input  [7:0] b,
  output [7:0] o
);

  assign o = a & b;  // AND_Gate and_1, 8 bits wide
endmodule

module or8 (
  input  [7:0] a,
  input  [7:0] b,
  output [7:0] o
);

  assign o = a | b;  // OR_Gate or_1, 8 bits wide
endmodule

module shl8 (
  input  [7:0] a,
  output [7:0] o
);

  // NoConnect on a[7]

  assign o = {a[6:0], 1'b0};
endmodule

module shr8 (
  input  [7:0] a,
  output [7:0] o
);

  // NoConnect on a[0]

  assign o = {1'b0, a[7:1]};
endmodule

module half_add (
  input  a,
  input  b,
  output sum,
  output carry
);

  xor2 xor2_1 (.i_0(a), .i_1(b), .o(sum));
  and and_1 (carry, b, a);
endmodule

module full_add (
  input  c_in,
  input  a,
  input  b,
  output sum,
  output c_out
);

  wire half_add_1_carry, half_add_1_sum, half_add_2_carry;

  half_add half_add_1 (.a(a), .b(b), .sum(half_add_1_sum), .carry(half_add_1_carry));
  half_add half_add_2 (.a(c_in), .b(half_add_1_sum), .sum(sum), .carry(half_add_2_carry));
  or or_1 (c_out, half_add_2_carry, half_add_1_carry);
endmodule

module full_add8 (
  input  [7:0] a,
  input  [7:0] b,
  output [7:0] sum,
  output c_out
);

  wire full_add_1_c_out, full_add_2_c_out, full_add_3_c_out, full_add_4_c_out, full_add_5_c_out,
       full_add_6_c_out, half_add_1_carry;

  half_add half_add_1 (.a(b[0]), .b(a[0]), .sum(sum[0]), .carry(half_add_1_carry));
  full_add full_add_1 (.c_in(half_add_1_carry), .a(b[1]), .b(a[1]), .sum(sum[1]), .c_out(full_add_1_c_out));
  full_add full_add_2 (.c_in(full_add_1_c_out), .a(b[2]), .b(a[2]), .sum(sum[2]), .c_out(full_add_2_c_out));
  full_add full_add_3 (.c_in(full_add_2_c_out), .a(b[3]), .b(a[3]), .sum(sum[3]), .c_out(full_add_3_c_out));
  full_add full_add_4 (.c_in(full_add_3_c_out), .a(b[4]), .b(a[4]), .sum(sum[4]), .c_out(full_add_4_c_out));
  full_add full_add_5 (.c_in(full_add_4_c_out), .a(b[5]), .b(a[5]), .sum(sum[5]), .c_out(full_add_5_c_out));
  full_add full_add_6 (.c_in(full_add_5_c_out), .a(b[6]), .b(a[6]), .sum(sum[6]), .c_out(full_add_6_c_out));
  full_add full_add_7 (.c_in(full_add_6_c_out), .a(b[7]), .b(a[7]), .sum(sum[7]), .c_out(c_out));
endmodule

module reg_a (
  input  clk,
  input  [7:0] i,
  output [7:0] o
);

  reg8 reg8_1 (.clk(clk), .i(i), .o(o));
endmodule

module reg_b (
  input  clk,
  input  [7:0] i,
  output [7:0] o
);

  reg8 reg8_1 (.clk(clk), .i(i), .o(o));
endmodule

module reg8 (
  input  clk,
  input  [7:0] i,
  output [7:0] o
);

  D_Flip_Flop d_ff_1 (.D(i[0]), .clk(clk), .Q(o[0]));  // open: Qn, preset, reset
  D_Flip_Flop d_ff_2 (.D(i[1]), .clk(clk), .Q(o[1]));  // open: Qn, preset, reset
  D_Flip_Flop d_ff_3 (.D(i[2]), .clk(clk), .Q(o[2]));  // open: Qn, preset, reset
  D_Flip_Flop d_ff_4 (.D(i[3]), .clk(clk), .Q(o[3]));  // open: Qn, preset, reset
  D_Flip_Flop d_ff_5 (.D(i[4]), .clk(clk), .Q(o[4]));  // open: Qn, preset, reset
  D_Flip_Flop d_ff_6 (.D(i[5]), .clk(clk), .Q(o[5]));  // open: Qn, preset, reset
  D_Flip_Flop d_ff_7 (.D(i[6]), .clk(clk), .Q(o[6]));  // open: Qn, preset, reset
  D_Flip_Flop d_ff_8 (.D(i[7]), .clk(clk), .Q(o[7]));  // open: Qn, preset, reset
endmodule

module reg_out (
  input  clk,
  input  [7:0] i,
  output [7:0] o
);

  reg8 reg8_1 (.clk(clk), .i(i), .o(o));
endmodule

module memory (
  input  [7:0] addr,
  input  we,
  input  oe,
  input  clk,
  input  [7:0] write,
  output [7:0] read
);

  RAM ram_1 (.addr(addr), .we(we), .oe(oe), .clk(clk), .din(write), .dout(read));
endmodule
